# Fritzing sketch Gardenr (saved by Fritzing 0.9.3b)
circuit board: 5.54831cm x 4.76791cm
breadboards: 1

parts:
  MCP3008 = MCP3008 [package=dil16]
  SHT-21 = female pin header, 4 pins [form="♀ (female)"]
  LCD = female pin header, 4 pins [form="♀ (female)"]
  Raspberry_Pi = double row female pin header, 40 pins [form="♀ (female)"]
  SOIL = female pin header, 4 pins [form="♀ (female)"]

nets:
  N1: MCP3008.CH0, SOIL.pin1
  N2: MCP3008.DGND, SHT-21.pin4, LCD.pin4, Raspberry_Pi.pin8, SOIL.pin4
  N3: MCP3008.CS/SHDN, Raspberry_Pi.pin32
  N4: MCP3008.Din, Raspberry_Pi.pin11
  N5: MCP3008.Dout, Raspberry_Pi.pin10
  N6: MCP3008.CLK, Raspberry_Pi.pin9
  N7: MCP3008.AGND, Raspberry_Pi.pin16
  N8: MCP3008.VREF, MCP3008.VDD, Raspberry_Pi.pin20
  N9: SHT-21.pin1, LCD.pin1, Raspberry_Pi.pin18
  N10: SHT-21.pin2, LCD.pin2, Raspberry_Pi.pin19
  N11: SHT-21.pin3, Raspberry_Pi.pin12
  N12: LCD.pin3, Raspberry_Pi.pin21, SOIL.pin3

notes:
  Gardenr
  GND
  5V
  3V3
  SDA
  SCL
  D0
  A0
  Designed by: Ameer Dawood
  Gardenr R2
  https://gardenr.ameer.io
  ... with ❤ for Aani & Nimra
