# Fritzing sketch Inverted_Switch (saved by Fritzing 0.9.3b)
breadboards: 1

parts:
  R1 = Resistor [tolerance=±5% resistance=100k package=THT]
  Q2 = NPN-Transistor [package="TO92 [THT]"]
  LED1 = LED - 5mm [color="Red (633nm)" package="5 mm [THT]"]
  S1 = Pushbutton [package="[THT]"]
  Battery = BATTERY-2 [package=battery-aaa]

nets:
  N1: R1.Pin_0, Q2.B, S1.Pin_3, S1.Pin_4
  N2: R1.Pin_1, LED1.anode, Battery.+1
  N3: Q2.E, S1.Pin_2, Battery.-1
  N4: Q2.C, LED1.cathode
