# Fritzing sketch LED_Breather_Using_IC_555 (saved by Fritzing 0.9.2b)
breadboards: 1

parts:
  U1 = 555 Timer [package="DIP8 [THT]"]
  Q1 = NPN-Transistor [package="TO92 [THT]"]
  LED1 = LED - 5mm [color="Red (633nm)" package="5 mm [THT]"]
  R1 = Resistor [tolerance=±5% resistance=150 package=THT]
  R2 = Resistor [tolerance=±5% resistance=1.2k package=THT]
  C1 = Electrolytic Capacitor [capacitance=1mF voltage=6.3V package="100 mil [THT, electrolytic]"]
  VCC1 = Battery block 9V

nets:
  N1: U1.Ground, LED1.cathode, C1.-, VCC1.-
  N2: U1.Output, R2.Pin_0
  N3: U1.Reset, U1.Vcc_Supply_Voltage, Q1.E, VCC1.+
  N4: U1.Threshold, Q1.B, R2.Pin_1, C1.+
  N5: Q1.C, R1.Pin_1
  N6: LED1.anode, R1.Pin_0
